# Fritzing sketch SpeedRacer (saved by Fritzing 0.9.3b)
breadboards: 1

parts:
  Part1 = Arduino Uno (Rev3)
  LCD1 = LCD screen
  LCD2 = LCD screen
  Part2 = Thumb Joystick

nets:
  N1: Part1.A1, Part2.HORZ
  N2: Part1.A2, Part2.VERT
  N3: Part1.A4/SDA, LCD1.V0, LCD2.V0
  N4: Part1.A5/SCL, LCD1.RS, LCD2.RS
  N5: Part1.D7, Part2.SEL
  VDD: Part1.5V, LCD1.VDD, LCD2.VDD, Part2.VCC
  GND: Part1.GND, LCD1.VSS, LCD2.VSS, Part2.GND
